# Fritzing sketch vwcdcemu_attiny85 (saved by Fritzing 0.9.3b)
circuit board: 8.46667cm x 5.64444cm
perfboards: 1

parts:
  U1 = Voltage Regulator - 5V [package="TO220 [THT]"]
  C1 = Electrolytic Capacitor [capacitance=4.7µF package="100 mil [THT, electrolytic]"]
  R1 = Resistor [tolerance=±5% resistance=3.3k package=THT]
  R2 = Resistor [tolerance=±5% resistance=3.3k package=THT]
  R3 = Resistor [tolerance=±5% resistance=3.3k package=THT]
  LED1 = LED - 5mm [color="Red (633nm)" package="5 mm [THT]"]
  U2 = attiny85 [package=dip]
  R5 = Resistor [tolerance=±5% resistance=10k package=THT]
  C2 = Electrolytic Capacitor [capacitance=1µF package="100 mil [THT, electrolytic]"]
  J2 = Generic female header - 5 pins [form="♀ (female)" package=THT]
  R4 = Resistor [tolerance=±5% resistance=220 package=THT]

nets:
  N1: U1.input_voltage, J2.VCDC12
  GND: U1.GND, C1.-, J2.GND, R4.Pin_0
  N2: U1.output_voltage, C1.+, LED1.anode, U2.Pin_8, R5.Pin_1
  N3: R1.Pin_0, J2.DTO
  N4: R1.Pin_1, U2.Pin_7
  N5: R2.Pin_0, J2.CLK
  N6: R2.Pin_1, U2.Pin_6
  N7: R3.Pin_0, J2.DTI
  N8: R3.Pin_1, U2.Pin_5
  N9: LED1.cathode, R4.Pin_1
  N10: U2.Pin_1, R5.Pin_0, C2.+
  N11: U2.Pin_4, C2.-

notes:
  GND
  DTI
  CLK
  DTO
  12V

custom parts:
  Generic female header - 5 pins: Generic female header
